# Fritzing sketch facial_req_schematic (saved by Fritzing 0.9.9b)
breadboards: 2

parts:
  Part1 = Arduino Uno (Rev3)
  Raspberry_Pi1 = Raspberry Pi B+
  LCD1 = LCD screen
  U1 = POT [package=3362u]
  LED1 = smd LED [color="Red (633nm)" package="1206 [SMD]"]
  LED2 = smd LED [color="Red (633nm)" package="1206 [SMD]"]

nets:
  N1: Part1.D11_PWM/MOSI, LCD1.E
  N2: Part1.D12/MISO, LCD1.RS
  N3: Part1.D2, LCD1.DB4
  N4: Part1.D3_PWM, LCD1.DB5
  N5: Part1.D4, LCD1.DB6
  N6: Part1.D5_PWM, LCD1.DB7
  5V: Part1.5V, LCD1.VDD, LCD1.LED+, U1.A
  GND: Part1.GND, LCD1.VSS, LCD1.R/W, LCD1.LED-, U1.E
  N7: Raspberry_Pi1.GPIO4, LED2.anode
  N8: Raspberry_Pi1.GPIO27, LED1.anode
  N9: Raspberry_Pi1.GND, LED1.cathode, LED2.cathode
  N10: LCD1.V0, U1.S
