# Fritzing sketch Project_Schematic (saved by Fritzing 0.9.9b)
breadboards: 1

parts:
  Part1 = Arduino Uno (Rev3)
  LCD1 = LCD screen
  U1 = POT [package=alps_pot]
  LED2 = smd LED [color="Red (633nm)" package="0805 [SMD]"]
  LED3 = smd LED [color="Red (633nm)" package="0805 [SMD]"]
  R1 = Resistor [tolerance=±5% power=0.25 resistance=220 package=THT]
  LED4 = smd LED [color="Red (633nm)" package="0805 [SMD]"]
  R2 = Resistor [tolerance=±5% power=0.25 resistance=220 package=THT]
  R3 = Resistor [tolerance=±5% power=0.25 resistance=220 package=THT]
  LED5 = smd LED [color="Red (633nm)" package="0805 [SMD]"]
  R4 = Resistor [tolerance=±5% power=0.25 resistance=220 package=THT]
  LED6 = smd LED [color="Red (633nm)" package="0805 [SMD]"]
  R5 = Resistor [tolerance=±5% power=0.25 resistance=220 package=THT]

nets:
  N1: Part1.A0, R5.Pin_1
  N2: Part1.A1, R4.Pin_1
  N3: Part1.A2, R3.Pin_1
  N4: Part1.A3, R2.Pin_1
  N5: Part1.A4/SDA, R1.Pin_1
  N6: Part1.D11_PWM/MOSI, LCD1.E
  N7: Part1.D12/MISO, LCD1.RS
  N8: Part1.D2, LCD1.DB7
  N9: Part1.D3_PWM, LCD1.DB6
  N10: Part1.D4, LCD1.DB5
  N11: Part1.D5_PWM, LCD1.DB4
  5V: Part1.5V, LCD1.VDD, LCD1.LED+, U1.E
  GND: Part1.GND, LCD1.VSS, LCD1.R/W, LCD1.LED-, U1.A, LED2.cathode, LED3.cathode, LED4.cathode, LED5.cathode, LED6.cathode
  N12: LCD1.V0, U1.S
  N13: LED2.anode, R3.Pin_0
  N14: LED3.anode, R1.Pin_0
  N15: LED4.anode, R2.Pin_0
  N16: LED5.anode, R4.Pin_0
  N17: LED6.anode, R5.Pin_0
